# Fritzing sketch esquema conexión adxl335 raspberrypi mcp3008 (saved by Fritzing 0.8.3b)
breadboards: 1

parts:
  Raspberry_Pi_rev1 = Raspberry Pi rev1
  IC1 = MCP3008 8-channel 10-bit ADC [part_number=MCP3008]
  Parte1 = Triple Axis Accelerometer Breakout - ADXL335

nets:
  3V3: Raspberry_Pi_rev1.3V3, IC1.no_name_yet#15, IC1.no_name_yet#16, Parte1.VCC
  GND: Raspberry_Pi_rev1.GND, IC1.no_name_yet#9, IC1.no_name_yet#14, Parte1.GND
  N1: Raspberry_Pi_rev1.GPIO_18, IC1.no_name_yet#10
  N2: Raspberry_Pi_rev1.GPIO4, IC1.no_name_yet#11
  N3: Raspberry_Pi_rev1.GPIO_24, IC1.no_name_yet#12
  N4: Raspberry_Pi_rev1.GPIO_25, IC1.no_name_yet#13
  N5: IC1.no_name_yet#1, Parte1.XOUT
  N6: IC1.no_name_yet#2, Parte1.YOUT
  N7: IC1.no_name_yet#3, Parte1.ZOUT

notes:
  MCP3008 COLOR HEADER Q2W GPIO
  CLK AMARILLO 22 6
  DOUT (MISO) VERDE 18 5
  DIN (MOSI) GRIS 16 4
  CS BLANCO 12 1
